// Logisim project Project.circ as structural Verilog: 26 circuits, main circuit Register_8b_locked
module main (
  input  in_1,
  input  in_2,
  input  in_3,
  input  in_4,
  input  in_5,
  input  in_6,
  input  in_7,
  input  in_8,
  input  in_9,
  input  in_10,
  input  in_11,
  input  EXTERMINATE,
  input  in_13
);

  wire ALUOVERFLOW, ALUZERO, and_1_out, and_2_out, and_3_out, clock_1_out, clockcontrol_1_out_5,
       controlunit_1_reset, controlunit_1_stop, EOP, not_1_out, or_2_out, PRINT, READ, ROMCLK, ROMDONE,
       s_r_ff_1_q, STOP;
  wire [1:0] A, ALUOP, controlunit_1_out_5, controlunit_1_out_6, controlunit_1_out_8, controlunit_1_out_15,
       dpath_fetch_1_out_2, dpath_fetch_1_out_5, dpath_fetch_1_out_6, dpath_fetch_1_out_7, IR, L, MAR, MBR,
       or_1_out, PC, PCCOUNT, programrom_1_out_7, R, RA, RAM, RD, S0, S1;
  wire [3:0] bcd_convert_1_out_2, bcd_convert_1_out_3, bcd_convert_1_out_4, PHASE, phaseclock_1_out_4,
       register_4b_1_out_6, register_4b_1_out_7, register_4b_2_out_6, register_4b_2_out_7,
       register_4b_3_out_6, register_4b_3_out_7;
  wire [6:0] segmentdecoder_1_out_3, segmentdecoder_2_out_3, segmentdecoder_3_out_3;
  wire [7:0] add_sub_8bits_1_r, alu_1_out_4, inputrom_1_out_11, IR_out_6, IR_out_7, L_out_6, L_out_7,
       multiplexer_1_out, PC_out_6, PCCOUNT_out_6, PCCOUNT_out_7, programrom_1_data, R_out_6, R_out_7,
       RA_out_6, RA_out_7, RD_out_6, RD_out_7, REG0_out_6, REG1_out_6, register_8b_locked_1_out_6,
       register_8b_locked_2_out_6, register_8b_locked_3_out_6, register_8b_passin_1_out_5;

  Clock clock_1 (.out(clock_1_out));
  CLOCKCONTROL clockcontrol_1 (
    .ROM_STATUS(ROMDONE), .in_1(clock_1_out), .ROM_ON(in_13), .STOP(STOP), .out_5(clockcontrol_1_out_5),
    .ROM_CLOCK(ROMCLK));
  Register_8b_locked u_RD (
    .out_7(RD_out_7), .R_W_Mode(RD[0]), .Address_Bit(RD[1]), .in_3(RD_out_7), .Clock(clockcontrol_1_out_5),
    .out_6(RD_out_6), .RESET(EXTERMINATE));
  // Probe on RD_out_6
  Register_8b_locked u_RA (
    .out_7(RA_out_7), .R_W_Mode(RA[0]), .Address_Bit(RA[1]), .in_3(RD_out_7), .Clock(clockcontrol_1_out_5),
    .out_6(RA_out_6), .RESET(EXTERMINATE));
  // Probe on RA_out_6
  assign or_1_out = RAM | programrom_1_out_7;  // OR_Gate or_1, 2 bits wide
  INPUTROM inputrom_1 (
    .in_9(in_9), .in_6(in_6), .in_7(in_7), .in_4(in_4), .in_5(in_5), .in_2(in_2), .in_3(in_3), .in_1(in_1),
    .in_8(in_8), .in_10(in_10), .out_11(inputrom_1_out_11));
  // Probe on RA_out_7[3:0]
  // Probe on RD_out_7
  PROGRAMROM programrom_1 (
    .out_5(RA_out_7[3:0]), .clk(ROMCLK), .DATA(programrom_1_data), .out_7(programrom_1_out_7),
    .out_6(ROMDONE), .ROM_INPUT(in_13), .in_3(EXTERMINATE));
  // Probe on register_8b_passin_1_out_5
  // Probe on RD_out_7
  Ram_16B ram_16b_1 (
    .SYSCLOCK(clockcontrol_1_out_5), .in_7(RA_out_7[3:0]), .in_2(RD_out_7), .in_1(or_1_out[0]),
    .out_11(RD_out_7), .in_6(or_1_out[1]), .CLEAR(EXTERMINATE), .ROMCLOCK(ROMCLK), .ROM_ON(in_13),
    .in_3(programrom_1_data), .ROM_DONE(ROMDONE));
  BCD_Convert bcd_convert_1 (
    .in_1(RD_out_7), .out_2(bcd_convert_1_out_2), .out_3(bcd_convert_1_out_3), .out_4(bcd_convert_1_out_4));
  // Probe on RD_out_7
  Register_8b_passin register_8b_passin_1 (
    .out_6(RD_out_7), .in_3(inputrom_1_out_11), .Address_Bit(READ), .Clock(clockcontrol_1_out_5),
    .out_5(register_8b_passin_1_out_5), .in_4(EXTERMINATE));
  // Probe on {register_8b_locked_1_out_6[7:5], EOP, register_8b_locked_1_out_6[3:0]}
  and and_1 (and_1_out, RD_out_7[7], PRINT);
  S_R_Flip_Flop s_r_ff_1 (
    .S(and_1_out), .R(and_2_out), .clk(clockcontrol_1_out_5), .Q(s_r_ff_1_q), .reset(EXTERMINATE));  // open: Qn, preset
  and and_2 (and_2_out, ~RD_out_7[7], PRINT);  // AND_Gate
  Register_8b_locked register_8b_locked_1 (
    .out_7(RD_out_7), .R_W_Mode(MAR[0]), .Address_Bit(MAR[1]), .in_3(RD_out_7), .Clock(clockcontrol_1_out_5),
    .out_6({register_8b_locked_1_out_6[7:5], EOP, register_8b_locked_1_out_6[3:0]}), .RESET(EXTERMINATE));
  Register_4b register_4b_1 (
    .out_7(register_4b_1_out_7), .Clock(clockcontrol_1_out_5), .Address_Bit(PRINT), .R_Mode(PRINT),
    .in_3(bcd_convert_1_out_2), .out_6(register_4b_1_out_6), .in_5(EXTERMINATE));
  // Probe on register_4b_1_out_6
  Register_4b register_4b_2 (
    .out_7(register_4b_2_out_7), .Clock(clockcontrol_1_out_5), .Address_Bit(PRINT), .R_Mode(PRINT),
    .in_3(bcd_convert_1_out_3), .out_6(register_4b_2_out_6), .in_5(EXTERMINATE));
  // Probe on register_4b_2_out_6
  Register_4b register_4b_3 (
    .out_7(register_4b_3_out_7), .Clock(clockcontrol_1_out_5), .Address_Bit(PRINT), .R_Mode(PRINT),
    .in_3(bcd_convert_1_out_4), .out_6(register_4b_3_out_6), .in_5(EXTERMINATE));
  // Probe on register_4b_3_out_6
  Register_8b_locked u_PCCOUNT (
    .out_7(PCCOUNT_out_7), .R_W_Mode(PCCOUNT[0]), .Address_Bit(PCCOUNT[1]), .in_3(add_sub_8bits_1_r),
    .Clock(clockcontrol_1_out_5), .out_6(PCCOUNT_out_6), .RESET(EXTERMINATE));
  // Probe on PCCOUNT_out_7
  and and_3 (and_3_out, PHASE[0], ~PHASE[1], ~PHASE[2], ~PHASE[3]);  // AND_Gate
  SegmentDecoder segmentdecoder_1 (.out_3(segmentdecoder_1_out_3), .in_1(register_4b_1_out_7), .in_2(s_r_ff_1_q));
  SegmentDecoder segmentdecoder_2 (.out_3(segmentdecoder_2_out_3), .in_1(register_4b_2_out_7), .in_2(s_r_ff_1_q));
  SegmentDecoder segmentdecoder_3 (.out_3(segmentdecoder_3_out_3), .in_1(register_4b_3_out_7), .in_2(s_r_ff_1_q));
  // Probe on PCCOUNT_out_6
  not not_1 (not_1_out, and_3_out);
  // Probe on register_8b_locked_2_out_6
  // Probe on REG0_out_6
  // Probe on REG1_out_6
  _7_Segment_Display u_7_segment_display_1 (
    .g(segmentdecoder_1_out_3[3]), .f(segmentdecoder_1_out_3[2]), .a(segmentdecoder_1_out_3[1]),
    .b(segmentdecoder_1_out_3[0]), .e(segmentdecoder_1_out_3[4]), .d(segmentdecoder_1_out_3[5]),
    .c(segmentdecoder_1_out_3[6]));  // open: dp
  Multiplexer #(.width(8), .enable("false")) multiplexer_1 (
    .in0(PCCOUNT_out_7), .in1(RD_out_7), .out(multiplexer_1_out), .sel(not_1_out));
  Register_8b_locked register_8b_locked_2 (
    .out_7(RD_out_7), .R_W_Mode(MBR[0]), .Address_Bit(MBR[1]), .in_3(RD_out_7), .Clock(clockcontrol_1_out_5),
    .out_6(register_8b_locked_2_out_6), .RESET(EXTERMINATE));
  Register_8b_locked REG0 (
    .out_7(RD_out_7), .R_W_Mode(S0[0]), .Address_Bit(S0[1]), .in_3(RD_out_7), .Clock(clockcontrol_1_out_5),
    .out_6(REG0_out_6), .RESET(EXTERMINATE));
  Register_8b_locked REG1 (
    .out_7(RD_out_7), .R_W_Mode(S1[0]), .Address_Bit(S1[1]), .in_3(RD_out_7), .Clock(clockcontrol_1_out_5),
    .out_6(REG1_out_6), .RESET(EXTERMINATE));
  _7_Segment_Display u_7_segment_display_2 (
    .g(segmentdecoder_2_out_3[3]), .f(segmentdecoder_2_out_3[2]), .a(segmentdecoder_2_out_3[1]),
    .b(segmentdecoder_2_out_3[0]), .e(segmentdecoder_2_out_3[4]), .d(segmentdecoder_2_out_3[5]),
    .c(segmentdecoder_2_out_3[6]));  // open: dp
  Add_Sub_8Bits add_sub_8bits_1 (
    .Add_Sub(1'b1), .A(RD_out_7), .B(8'h1), .R(add_sub_8bits_1_r));  // open: Zero, Overflow
  // Probe on multiplexer_1_out
  Register_8b_locked u_PC (
    .out_7(RD_out_7), .R_W_Mode(PC[0]), .Address_Bit(PC[1]), .in_3(multiplexer_1_out),
    .Clock(clockcontrol_1_out_5), .out_6(PC_out_6), .RESET(EXTERMINATE));
  // Probe on PC_out_6
  _7_Segment_Display u_7_segment_display_3 (
    .g(segmentdecoder_3_out_3[3]), .f(segmentdecoder_3_out_3[2]), .a(segmentdecoder_3_out_3[1]),
    .b(segmentdecoder_3_out_3[0]), .e(segmentdecoder_3_out_3[4]), .d(segmentdecoder_3_out_3[5]),
    .c(segmentdecoder_3_out_3[6]));  // open: dp
  // Probe on R_out_6
  // Probe on L_out_6
  // Probe on phaseclock_1_out_4
  or or_2 (or_2_out, controlunit_1_reset, EXTERMINATE, in_11);
  Register_8b_passthrough u_R (
    .in_3(RD_out_7), .out_7(R_out_7), .Address_Bit(R[1]), .R_W_Mode(R[0]), .out_6(R_out_6),
    .Clock(clockcontrol_1_out_5), .CLEAR(EXTERMINATE));
  Register_8b_passthrough u_L (
    .in_3(RD_out_7), .out_7(L_out_7), .Address_Bit(L[1]), .R_W_Mode(L[0]), .out_6(L_out_6),
    .Clock(clockcontrol_1_out_5), .CLEAR(EXTERMINATE));
  // Probe on IR_out_7
  Register_8b_passthrough u_IR (
    .in_3(RD_out_7), .out_7(IR_out_7), .Address_Bit(IR[1]), .R_W_Mode(IR[0]), .out_6(IR_out_6),
    .Clock(clockcontrol_1_out_5), .CLEAR(EXTERMINATE));
  // Probe on IR_out_6
  PHASECLOCK phaseclock_1 (.out_3(PHASE), .in_1(clockcontrol_1_out_5), .Reset(or_2_out), .out_4(phaseclock_1_out_4));
  CONTROLUNIT controlunit_1 (
    .out_11(S1), .in_2(PHASE), .out_10(S0), .out_8(controlunit_1_out_8), .out_5(controlunit_1_out_5),
    .in_1(IR_out_7), .out_4(RD_out_7), .out_6(controlunit_1_out_6), .RESET(controlunit_1_reset), .READ(READ),
    .PRINT(PRINT), .out_12(ALUOP), .out_13(L), .out_14(R), .out_16(A), .STOP(controlunit_1_stop),
    .out_15(controlunit_1_out_15), .in_3(ALUZERO));
  DPath_FETCH dpath_fetch_1 (
    .out_7(dpath_fetch_1_out_7), .out_5(dpath_fetch_1_out_5), .in_1(PHASE), .out_4(MAR),
    .out_2(dpath_fetch_1_out_2), .out_9(IR), .out_8(MBR), .out_6(dpath_fetch_1_out_6), .out_3(PCCOUNT));
  ALU alu_1 (.out_4(alu_1_out_4), .out_5(ALUZERO), .in_2(R_out_7), .in_3(L_out_7), .out_6(ALUOVERFLOW), .in_1(ALUOP));
  Register_8b_locked register_8b_locked_3 (
    .out_7(RD_out_7), .R_W_Mode(A[0]), .Address_Bit(A[1]), .in_3(alu_1_out_4), .Clock(clockcontrol_1_out_5),
    .out_6(register_8b_locked_3_out_6), .RESET(EXTERMINATE));
  // Probe on register_8b_locked_3_out_6
  assign RA = controlunit_1_out_6 | dpath_fetch_1_out_5;  // OR_Gate or_3, 2 bits wide
  assign RD = controlunit_1_out_5 | dpath_fetch_1_out_7;  // OR_Gate or_4, 2 bits wide
  or or_5 (STOP, EOP, EXTERMINATE, controlunit_1_stop);
  assign RAM = controlunit_1_out_8 | dpath_fetch_1_out_6;  // OR_Gate or_6, 2 bits wide
  assign PC = dpath_fetch_1_out_2 | controlunit_1_out_15;  // OR_Gate or_7, 2 bits wide

  // Other names for the same wires on the sheet: DALEK_EXTERMINATE_PRIMATIVE_CIRCUIT = EXTERMINATE; ROMON = in_13

  // Notes on the sheet:
  //   Data
  //   Address
  //   MAR
  //   DATA
  //   MBR
  //   ON = 0/ OFF =1
  //   READ ROM
endmodule

module Register_8b_locked (
  input  Address_Bit,
  input  Clock,
  input  [7:0] in_3,
  input  R_W_Mode,
  input  RESET,
  output [7:0] out_6,
  output [7:0] out_7
);

  wire and_1_out, and_2_out, and_3_out, and_4_out, and_5_out, and_6_out, and_7_out, and_8_out, and_9_out,
       and_10_out, and_11_out, and_12_out, and_13_out, and_14_out, and_15_out, and_16_out, and_17_out,
       and_18_out, and_19_out, and_20_out, and_21_out, and_22_out, and_23_out, and_24_out, and_25_out,
       and_26_out, controlled_buffer_1_out, controlled_buffer_2_out, controlled_buffer_3_out,
       controlled_buffer_4_out, controlled_buffer_5_out, controlled_buffer_6_out, controlled_buffer_7_out,
       controlled_buffer_8_out, not_1_out;

  assign controlled_buffer_1_out = and_1_out ? in_3[0] : 1'bz;  // Controlled_Buffer controlled_buffer_1
  assign controlled_buffer_2_out = and_1_out ? in_3[1] : 1'bz;  // Controlled_Buffer controlled_buffer_2
  assign controlled_buffer_3_out = and_1_out ? in_3[2] : 1'bz;  // Controlled_Buffer controlled_buffer_3
  assign controlled_buffer_4_out = and_1_out ? in_3[3] : 1'bz;  // Controlled_Buffer controlled_buffer_4
  assign controlled_buffer_5_out = and_1_out ? in_3[4] : 1'bz;  // Controlled_Buffer controlled_buffer_5
  assign controlled_buffer_6_out = and_1_out ? in_3[5] : 1'bz;  // Controlled_Buffer controlled_buffer_6
  assign controlled_buffer_7_out = and_1_out ? in_3[6] : 1'bz;  // Controlled_Buffer controlled_buffer_7
  assign controlled_buffer_8_out = and_1_out ? in_3[7] : 1'bz;  // Controlled_Buffer controlled_buffer_8
  and and_1 (and_1_out, Address_Bit, R_W_Mode);
  and and_2 (and_2_out, controlled_buffer_1_out, R_W_Mode, 1'b1);
  and and_3 (and_3_out, ~controlled_buffer_1_out, R_W_Mode, 1'b1);  // AND_Gate
  and and_4 (and_4_out, controlled_buffer_2_out, R_W_Mode, 1'b1);
  and and_5 (and_5_out, ~controlled_buffer_2_out, R_W_Mode, 1'b1);  // AND_Gate
  and and_6 (and_6_out, controlled_buffer_3_out, R_W_Mode, 1'b1);
  and and_7 (and_7_out, ~controlled_buffer_3_out, R_W_Mode, 1'b1);  // AND_Gate
  and and_8 (and_8_out, controlled_buffer_4_out, R_W_Mode, 1'b1);
  and and_9 (and_9_out, ~controlled_buffer_4_out, R_W_Mode, 1'b1);  // AND_Gate
  and and_10 (and_10_out, controlled_buffer_5_out, R_W_Mode, 1'b1);
  and and_11 (and_11_out, ~controlled_buffer_5_out, R_W_Mode, 1'b1);  // AND_Gate
  and and_12 (and_12_out, controlled_buffer_6_out, R_W_Mode, 1'b1);
  and and_13 (and_13_out, ~controlled_buffer_6_out, R_W_Mode, 1'b1);  // AND_Gate
  and and_14 (and_14_out, controlled_buffer_7_out, R_W_Mode, 1'b1);
  and and_15 (and_15_out, ~controlled_buffer_7_out, R_W_Mode, 1'b1);  // AND_Gate
  and and_16 (and_16_out, controlled_buffer_8_out, R_W_Mode, 1'b1);
  and and_17 (and_17_out, ~controlled_buffer_8_out, R_W_Mode, 1'b1);  // AND_Gate
  S_R_Flip_Flop s_r_ff_1 (.S(and_2_out), .R(and_3_out), .clk(Clock), .Q(out_6[0]), .reset(RESET));  // open: Qn, preset
  S_R_Flip_Flop s_r_ff_2 (.S(and_4_out), .R(and_5_out), .clk(Clock), .Q(out_6[1]), .reset(RESET));  // open: Qn, preset
  S_R_Flip_Flop s_r_ff_3 (.S(and_6_out), .R(and_7_out), .clk(Clock), .Q(out_6[2]), .reset(RESET));  // open: Qn, preset
  S_R_Flip_Flop s_r_ff_4 (.S(and_8_out), .R(and_9_out), .clk(Clock), .Q(out_6[3]), .reset(RESET));  // open: Qn, preset
  S_R_Flip_Flop s_r_ff_5 (
    .S(and_10_out), .R(and_11_out), .clk(Clock), .Q(out_6[4]), .reset(RESET));  // open: Qn, preset
  S_R_Flip_Flop s_r_ff_6 (
    .S(and_12_out), .R(and_13_out), .clk(Clock), .Q(out_6[5]), .reset(RESET));  // open: Qn, preset
  S_R_Flip_Flop s_r_ff_7 (
    .S(and_14_out), .R(and_15_out), .clk(Clock), .Q(out_6[6]), .reset(RESET));  // open: Qn, preset
  S_R_Flip_Flop s_r_ff_8 (
    .S(and_16_out), .R(and_17_out), .clk(Clock), .Q(out_6[7]), .reset(RESET));  // open: Qn, preset
  not not_1 (not_1_out, R_W_Mode);
  assign out_7[0] = and_26_out ? and_18_out : 1'bz;  // Controlled_Buffer controlled_buffer_9
  and and_18 (and_18_out, out_6[0], Address_Bit, not_1_out);
  and and_19 (and_19_out, out_6[1], Address_Bit, not_1_out);
  assign out_7[1] = and_26_out ? and_19_out : 1'bz;  // Controlled_Buffer controlled_buffer_10
  and and_20 (and_20_out, out_6[2], Address_Bit, not_1_out);
  assign out_7[2] = and_26_out ? and_20_out : 1'bz;  // Controlled_Buffer controlled_buffer_11
  assign out_7[3] = and_26_out ? and_21_out : 1'bz;  // Controlled_Buffer controlled_buffer_12
  and and_21 (and_21_out, out_6[3], Address_Bit, not_1_out);
  and and_22 (and_22_out, out_6[4], Address_Bit, not_1_out);
  assign out_7[4] = and_26_out ? and_22_out : 1'bz;  // Controlled_Buffer controlled_buffer_13
  and and_23 (and_23_out, out_6[5], Address_Bit, not_1_out);
  assign out_7[5] = and_26_out ? and_23_out : 1'bz;  // Controlled_Buffer controlled_buffer_14
  assign out_7[6] = and_26_out ? and_24_out : 1'bz;  // Controlled_Buffer controlled_buffer_15
  and and_24 (and_24_out, out_6[6], Address_Bit, not_1_out);
  assign out_7[7] = and_26_out ? and_25_out : 1'bz;  // Controlled_Buffer controlled_buffer_16
  and and_25 (and_25_out, out_6[7], Address_Bit, not_1_out);
  and and_26 (and_26_out, Address_Bit, not_1_out);
  // Probe on out_6

  // Notes on the sheet:
  //   Probe
endmodule

module SegmentDecoder (
  input  [3:0] in_1,
  input  in_2,
  output [6:0] out_3
);

  wire decoder_1_out0, decoder_1_out1, decoder_1_out2, decoder_1_out3, decoder_1_out4, decoder_1_out5,
       decoder_1_out6, decoder_1_out7, decoder_1_out8, decoder_1_out9, not_1_out;
  wire [3:0] controlled_buffer_1_out;

  assign controlled_buffer_1_out = not_1_out ? in_1 : 4'bz;  // Controlled_Buffer controlled_buffer_1
  not not_1 (not_1_out, in_2);
  Decoder #(.select(4)) decoder_1 (
    .out0(decoder_1_out0), .out1(decoder_1_out1), .out2(decoder_1_out2), .out3(decoder_1_out3),
    .out4(decoder_1_out4), .out5(decoder_1_out5), .out6(decoder_1_out6), .out7(decoder_1_out7),
    .out8(decoder_1_out8), .out9(decoder_1_out9), .sel(controlled_buffer_1_out));  // open: out10, out11, out12, out13, out14, out15, en
  or or_1 (out_3[0], decoder_1_out0, decoder_1_out1, decoder_1_out2, decoder_1_out3, decoder_1_out4, decoder_1_out7, decoder_1_out8, decoder_1_out9);
  or or_2 (out_3[1], decoder_1_out0, decoder_1_out2, decoder_1_out3, decoder_1_out5, in_2, decoder_1_out6, decoder_1_out7, decoder_1_out8, decoder_1_out9);
  or or_3 (out_3[2], decoder_1_out0, decoder_1_out4, decoder_1_out5, decoder_1_out6, decoder_1_out8, decoder_1_out9, in_2);
  or or_4 (out_3[3], decoder_1_out9, decoder_1_out2, decoder_1_out3, decoder_1_out4, decoder_1_out5, decoder_1_out6, decoder_1_out8, in_2);
  or or_5 (out_3[4], decoder_1_out0, in_2, decoder_1_out2, decoder_1_out8, decoder_1_out6);
  or or_6 (out_3[5], decoder_1_out8, decoder_1_out0, decoder_1_out2, decoder_1_out3, decoder_1_out5, decoder_1_out6, in_2);
  or or_7 (out_3[6], decoder_1_out0, decoder_1_out1, decoder_1_out3, decoder_1_out4, decoder_1_out9, decoder_1_out5, decoder_1_out6, decoder_1_out7, decoder_1_out8);
  _7_Segment_Display u_7_segment_display_1 (
    .g(out_3[3]), .f(out_3[2]), .a(out_3[1]), .b(out_3[0]), .e(out_3[4]), .d(out_3[5]), .c(out_3[6]));  // open: dp

  // Notes on the sheet:
  //   Error Code
  //   top right
  //   top
  //   top left
  //   middle
  //   bottom left
  //   bottom
  //   bottom right
endmodule

module Ram_16B (
  input  in_1,
  input  [7:0] in_2,
  input  [7:0] in_3,
  input  ROM_ON,
  input  ROM_DONE,
  input  in_6,
  input  [3:0] in_7,
  input  ROMCLOCK,
  input  SYSCLOCK,
  input  CLEAR,
  output [7:0] out_11
);

  wire and_1_out, and_2_out, and_3_out, decoder_1_out0, decoder_1_out1, decoder_1_out2, decoder_1_out3,
       decoder_2_out0, decoder_2_out1, decoder_2_out2, decoder_2_out3, decoder_3_out0, decoder_3_out1,
       decoder_3_out2, decoder_3_out3, decoder_4_out0, decoder_4_out1, decoder_4_out2, decoder_4_out3,
       decoder_5_out0, decoder_5_out1, decoder_5_out2, decoder_5_out3, not_1_out, or_1_out;
  wire [1:0] controlled_buffer_3_out, controlled_buffer_4_out, controlled_buffer_5_out,
       controlled_buffer_6_out;
  wire [7:0] controlled_buffer_1_out, register_8b_locked_1_out_6, register_8b_locked_1_out_7,
       register_8b_locked_2_out_6, register_8b_locked_3_out_6, register_8b_locked_4_out_6,
       register_8b_locked_5_out_6, register_8b_locked_6_out_6, register_8b_locked_7_out_6,
       register_8b_locked_8_out_6, register_8b_locked_9_out_6, register_8b_locked_10_out_6,
       register_8b_locked_11_out_6, register_8b_locked_12_out_6, register_8b_locked_13_out_6,
       register_8b_locked_14_out_6, register_8b_locked_15_out_6, register_8b_locked_16_out_6;

  and and_1 (and_1_out, ROM_ON, ~ROM_DONE);  // AND_Gate
  assign controlled_buffer_1_out = and_1_out ? in_3 : 8'bz;  // Controlled_Buffer controlled_buffer_1
  not not_1 (not_1_out, and_1_out);
  assign controlled_buffer_1_out = and_2_out ? in_2 : 8'bz;  // Controlled_Buffer controlled_buffer_2
  and and_2 (and_2_out, in_6, not_1_out, in_1);
  Decoder #(.select(2)) decoder_1 (
    .out0(decoder_1_out0), .out1(decoder_1_out1), .out2(decoder_1_out2), .out3(decoder_1_out3),
    .sel(in_7[3:2]));  // open: en
  Decoder #(.select(2)) decoder_2 (
    .out0(decoder_2_out0), .out1(decoder_2_out1), .out2(decoder_2_out2), .out3(decoder_2_out3),
    .sel(controlled_buffer_3_out));  // open: en
  assign controlled_buffer_3_out = decoder_1_out0 ? in_7[1:0] : 2'bz;  // Controlled_Buffer controlled_buffer_3
  // Probe on controlled_buffer_1_out
  or or_1 (or_1_out, ROMCLOCK, SYSCLOCK);
  // Probe on register_8b_locked_1_out_6
  // Probe on register_8b_locked_2_out_6
  // Probe on register_8b_locked_3_out_6
  // Probe on register_8b_locked_4_out_6
  Register_8b_locked register_8b_locked_1 (
    .out_7(register_8b_locked_1_out_7), .R_W_Mode(in_1), .Address_Bit(decoder_2_out0),
    .in_3(controlled_buffer_1_out), .Clock(or_1_out), .out_6(register_8b_locked_1_out_6), .RESET(CLEAR));
  Register_8b_locked register_8b_locked_2 (
    .out_7(register_8b_locked_1_out_7), .R_W_Mode(in_1), .Address_Bit(decoder_2_out1),
    .in_3(controlled_buffer_1_out), .Clock(or_1_out), .out_6(register_8b_locked_2_out_6), .RESET(CLEAR));
  Register_8b_locked register_8b_locked_3 (
    .out_7(register_8b_locked_1_out_7), .R_W_Mode(in_1), .Address_Bit(decoder_2_out2),
    .in_3(controlled_buffer_1_out), .Clock(or_1_out), .out_6(register_8b_locked_3_out_6), .RESET(CLEAR));
  Register_8b_locked register_8b_locked_4 (
    .out_7(register_8b_locked_1_out_7), .R_W_Mode(in_1), .Address_Bit(decoder_2_out3),
    .in_3(controlled_buffer_1_out), .Clock(or_1_out), .out_6(register_8b_locked_4_out_6), .RESET(CLEAR));
  Decoder #(.select(2)) decoder_3 (
    .out0(decoder_3_out0), .out1(decoder_3_out1), .out2(decoder_3_out2), .out3(decoder_3_out3),
    .sel(controlled_buffer_4_out));  // open: en
  assign controlled_buffer_4_out = decoder_1_out1 ? in_7[1:0] : 2'bz;  // Controlled_Buffer controlled_buffer_4
  // Probe on register_8b_locked_5_out_6
  // Probe on register_8b_locked_6_out_6
  // Probe on register_8b_locked_7_out_6
  // Probe on register_8b_locked_8_out_6
  Register_8b_locked register_8b_locked_5 (
    .out_7(register_8b_locked_1_out_7), .R_W_Mode(in_1), .Address_Bit(decoder_3_out0),
    .in_3(controlled_buffer_1_out), .Clock(or_1_out), .out_6(register_8b_locked_5_out_6), .RESET(CLEAR));
  Register_8b_locked register_8b_locked_6 (
    .out_7(register_8b_locked_1_out_7), .R_W_Mode(in_1), .Address_Bit(decoder_3_out1),
    .in_3(controlled_buffer_1_out), .Clock(or_1_out), .out_6(register_8b_locked_6_out_6), .RESET(CLEAR));
  Register_8b_locked register_8b_locked_7 (
    .out_7(register_8b_locked_1_out_7), .R_W_Mode(in_1), .Address_Bit(decoder_3_out2),
    .in_3(controlled_buffer_1_out), .Clock(or_1_out), .out_6(register_8b_locked_7_out_6), .RESET(CLEAR));
  Register_8b_locked register_8b_locked_8 (
    .out_7(register_8b_locked_1_out_7), .R_W_Mode(in_1), .Address_Bit(decoder_3_out3),
    .in_3(controlled_buffer_1_out), .Clock(or_1_out), .out_6(register_8b_locked_8_out_6), .RESET(CLEAR));
  Decoder #(.select(2)) decoder_4 (
    .out0(decoder_4_out0), .out1(decoder_4_out1), .out2(decoder_4_out2), .out3(decoder_4_out3),
    .sel(controlled_buffer_5_out));  // open: en
  assign controlled_buffer_5_out = decoder_1_out2 ? in_7[1:0] : 2'bz;  // Controlled_Buffer controlled_buffer_5
  // Probe on register_8b_locked_9_out_6
  // Probe on register_8b_locked_10_out_6
  // Probe on register_8b_locked_11_out_6
  // Probe on register_8b_locked_12_out_6
  Register_8b_locked register_8b_locked_9 (
    .out_7(register_8b_locked_1_out_7), .R_W_Mode(in_1), .Address_Bit(decoder_4_out0),
    .in_3(controlled_buffer_1_out), .Clock(or_1_out), .out_6(register_8b_locked_9_out_6), .RESET(CLEAR));
  Register_8b_locked register_8b_locked_10 (
    .out_7(register_8b_locked_1_out_7), .R_W_Mode(in_1), .Address_Bit(decoder_4_out1),
    .in_3(controlled_buffer_1_out), .Clock(or_1_out), .out_6(register_8b_locked_10_out_6), .RESET(CLEAR));
  Register_8b_locked register_8b_locked_11 (
    .out_7(register_8b_locked_1_out_7), .R_W_Mode(in_1), .Address_Bit(decoder_4_out2),
    .in_3(controlled_buffer_1_out), .Clock(or_1_out), .out_6(register_8b_locked_11_out_6), .RESET(CLEAR));
  Register_8b_locked register_8b_locked_12 (
    .out_7(register_8b_locked_1_out_7), .R_W_Mode(in_1), .Address_Bit(decoder_4_out3),
    .in_3(controlled_buffer_1_out), .Clock(or_1_out), .out_6(register_8b_locked_12_out_6), .RESET(CLEAR));
  Decoder #(.select(2)) decoder_5 (
    .out0(decoder_5_out0), .out1(decoder_5_out1), .out2(decoder_5_out2), .out3(decoder_5_out3),
    .sel(controlled_buffer_6_out));  // open: en
  assign controlled_buffer_6_out = decoder_1_out3 ? in_7[1:0] : 2'bz;  // Controlled_Buffer controlled_buffer_6
  Register_8b_locked register_8b_locked_13 (
    .out_7(register_8b_locked_1_out_7), .R_W_Mode(in_1), .Address_Bit(decoder_5_out0),
    .in_3(controlled_buffer_1_out), .Clock(or_1_out), .out_6(register_8b_locked_13_out_6), .RESET(CLEAR));
  // Probe on register_8b_locked_13_out_6
  Register_8b_locked register_8b_locked_14 (
    .out_7(register_8b_locked_1_out_7), .R_W_Mode(in_1), .Address_Bit(decoder_5_out1),
    .in_3(controlled_buffer_1_out), .Clock(or_1_out), .out_6(register_8b_locked_14_out_6), .RESET(CLEAR));
  // Probe on register_8b_locked_14_out_6
  Register_8b_locked register_8b_locked_15 (
    .out_7(register_8b_locked_1_out_7), .R_W_Mode(in_1), .Address_Bit(decoder_5_out2),
    .in_3(controlled_buffer_1_out), .Clock(or_1_out), .out_6(register_8b_locked_15_out_6), .RESET(CLEAR));
  // Probe on register_8b_locked_15_out_6
  Register_8b_locked register_8b_locked_16 (
    .out_7(register_8b_locked_1_out_7), .R_W_Mode(in_1), .Address_Bit(decoder_5_out3),
    .in_3(controlled_buffer_1_out), .Clock(or_1_out), .out_6(register_8b_locked_16_out_6), .RESET(CLEAR));
  // Probe on register_8b_locked_16_out_6
  and and_3 (and_3_out, in_6, ~in_1);  // AND_Gate
  assign out_11 = and_3_out ? register_8b_locked_1_out_7 : 8'bz;  // Controlled_Buffer controlled_buffer_7

  // Notes on the sheet:
  //   ROM DATA
endmodule

module Ram_256B (
  input  in_1,
  input  [7:0] in_2,
  input  in_3,
  input  [7:0] in_4,
  output [7:0] out_5
);

  wire decoder_1_out0, decoder_1_out1, decoder_1_out2, decoder_1_out3;
  wire [3:0] controlled_buffer_1_out, controlled_buffer_2_out, controlled_buffer_3_out,
       controlled_buffer_4_out, demultiplexer_1_out0, demultiplexer_1_out1, demultiplexer_1_out2,
       demultiplexer_1_out3, demultiplexer_2_out0, demultiplexer_2_out1, demultiplexer_2_out2,
       demultiplexer_2_out3, demultiplexer_3_out0, demultiplexer_3_out1, demultiplexer_3_out2,
       demultiplexer_3_out3, demultiplexer_4_out0, demultiplexer_4_out1, demultiplexer_4_out2,
       demultiplexer_4_out3;

  // Probe on in_4[3:2]
  // Probe on in_4[1:0]
  Decoder #(.select(2)) decoder_1 (
    .out0(decoder_1_out0), .out1(decoder_1_out1), .out2(decoder_1_out2), .out3(decoder_1_out3),
    .sel(in_4[1:0]));  // open: en
  Demultiplexer #(.select(2), .width(4), .enable("false")) demultiplexer_1 (
    .out0(demultiplexer_1_out0), .out1(demultiplexer_1_out1), .out2(demultiplexer_1_out2),
    .out3(demultiplexer_1_out3), .in(controlled_buffer_1_out), .sel(in_4[3:2]));
  assign controlled_buffer_1_out = decoder_1_out0 ? in_4[7:4] : 4'bz;  // Controlled_Buffer controlled_buffer_1
  // Probe on in_4[7:4]
  // Ram_16B ram_16b_1: pin names not known; wires that end beside it: in_2, demultiplexer_1_out0, in_1, in_3, out_5
  // Ram_16B ram_16b_2: pin names not known; wires that end beside it: in_2, demultiplexer_1_out1, in_1, in_3, out_5
  // Ram_16B ram_16b_3: pin names not known; wires that end beside it: in_2, demultiplexer_1_out2, in_1, in_3, out_5
  // Ram_16B ram_16b_4: pin names not known; wires that end beside it: in_2, demultiplexer_1_out3, in_1, in_3, out_5
  Demultiplexer #(.select(2), .width(4), .enable("false")) demultiplexer_2 (
    .out0(demultiplexer_2_out0), .out1(demultiplexer_2_out1), .out2(demultiplexer_2_out2),
    .out3(demultiplexer_2_out3), .in(controlled_buffer_2_out), .sel(in_4[3:2]));
  assign controlled_buffer_2_out = decoder_1_out1 ? in_4[7:4] : 4'bz;  // Controlled_Buffer controlled_buffer_2
  // Ram_16B ram_16b_5: pin names not known; wires that end beside it: in_2, demultiplexer_2_out0, in_1, in_3, out_5, out_5
  Ram_16B ram_16b_6 (
    .SYSCLOCK(in_3), .in_7(demultiplexer_2_out1), .in_2(in_2), .in_1(in_1));  // open: out_11, in_6, CLEAR, ROMCLOCK, ROM_ON, in_3, ROM_DONE
  // Ram_16B ram_16b_7: pin names not known; wires that end beside it: in_2, demultiplexer_2_out2, in_1, in_3, out_5, out_5
  Ram_16B ram_16b_8 (
    .SYSCLOCK(in_3), .in_7(demultiplexer_2_out3), .in_2(in_2), .in_1(in_1));  // open: out_11, in_6, CLEAR, ROMCLOCK, ROM_ON, in_3, ROM_DONE
  assign controlled_buffer_3_out = decoder_1_out2 ? in_4[7:4] : 4'bz;  // Controlled_Buffer controlled_buffer_3
  Demultiplexer #(.select(2), .width(4), .enable("false")) demultiplexer_3 (
    .out0(demultiplexer_3_out0), .out1(demultiplexer_3_out1), .out2(demultiplexer_3_out2),
    .out3(demultiplexer_3_out3), .in(controlled_buffer_3_out), .sel(in_4[3:2]));
  // Ram_16B ram_16b_9: pin names not known; wires that end beside it: in_2, demultiplexer_3_out0, in_1, in_3, out_5, out_5
  Ram_16B ram_16b_10 (
    .SYSCLOCK(in_3), .in_7(demultiplexer_3_out1), .in_2(in_2), .in_1(in_1));  // open: out_11, in_6, CLEAR, ROMCLOCK, ROM_ON, in_3, ROM_DONE
  // Ram_16B ram_16b_11: pin names not known; wires that end beside it: in_2, demultiplexer_3_out2, in_1, in_3, out_5, out_5
  Ram_16B ram_16b_12 (
    .SYSCLOCK(in_3), .in_7(demultiplexer_3_out3), .in_2(in_2), .in_1(in_1));  // open: out_11, in_6, CLEAR, ROMCLOCK, ROM_ON, in_3, ROM_DONE
  Demultiplexer #(.select(2), .width(4), .enable("false")) demultiplexer_4 (
    .out0(demultiplexer_4_out0), .out1(demultiplexer_4_out1), .out2(demultiplexer_4_out2),
    .out3(demultiplexer_4_out3), .in(controlled_buffer_4_out), .sel(in_4[3:2]));
  assign controlled_buffer_4_out = decoder_1_out3 ? in_4[7:4] : 4'bz;  // Controlled_Buffer controlled_buffer_4
  // Ram_16B ram_16b_13: pin names not known; wires that end beside it: in_2, demultiplexer_4_out0, in_1, in_3, out_5, out_5
  Ram_16B ram_16b_14 (
    .SYSCLOCK(in_3), .in_7(demultiplexer_4_out1), .in_2(in_2), .in_1(in_1));  // open: out_11, in_6, CLEAR, ROMCLOCK, ROM_ON, in_3, ROM_DONE
  // Ram_16B ram_16b_15: pin names not known; wires that end beside it: in_2, demultiplexer_4_out2, in_1, in_3, out_5, out_5
  Ram_16B ram_16b_16 (
    .SYSCLOCK(in_3), .in_7(demultiplexer_4_out3), .in_2(in_2), .in_1(in_1));  // open: out_11, in_6, CLEAR, ROMCLOCK, ROM_ON, in_3, ROM_DONE
endmodule

module Add_Sub_8Bits (
  input  Add_Sub,
  input  [7:0] A,
  input  [7:0] B,
  output [7:0] R,
  output Zero,
  output Overflow
);

  wire add_1bit_1_cout, add_1bit_2_cout, add_1bit_3_cout, add_1bit_4_cout, add_1bit_5_cout, add_1bit_6_cout,
       add_1bit_7_cout, and_1_out, not_1_out;
  wire [7:0] bit_extender_1_out, not_2_out, xor_1_out;

  // Probe on A
  // Probe on B
  assign xor_1_out = B ^ bit_extender_1_out;  // XOR_Gate xor_1, 8 bits wide
  assign bit_extender_1_out = {{7{not_1_out}}, not_1_out};  // Bit_Extender bit_extender_1
  not not_1 (not_1_out, Add_Sub);
  Add_1Bit add_1bit_1 (.Sum(R[0]), .A(A[0]), .B(xor_1_out[0]), .Cout(add_1bit_1_cout), .Cin(not_1_out));
  Add_1Bit add_1bit_2 (.Sum(R[1]), .A(A[1]), .B(xor_1_out[1]), .Cout(add_1bit_2_cout), .Cin(add_1bit_1_cout));
  Add_1Bit add_1bit_3 (.Sum(R[2]), .A(A[2]), .B(xor_1_out[2]), .Cout(add_1bit_3_cout), .Cin(add_1bit_2_cout));
  Add_1Bit add_1bit_4 (.Sum(R[3]), .A(A[3]), .B(xor_1_out[3]), .Cout(add_1bit_4_cout), .Cin(add_1bit_3_cout));
  Add_1Bit add_1bit_5 (.Sum(R[4]), .A(A[4]), .B(xor_1_out[4]), .Cout(add_1bit_5_cout), .Cin(add_1bit_4_cout));
  Add_1Bit add_1bit_6 (.Sum(R[5]), .A(A[5]), .B(xor_1_out[5]), .Cout(add_1bit_6_cout), .Cin(add_1bit_5_cout));
  Add_1Bit add_1bit_7 (.Sum(R[6]), .A(A[6]), .B(xor_1_out[6]), .Cout(add_1bit_7_cout), .Cin(add_1bit_6_cout));
  Add_1Bit add_1bit_8 (.Sum(R[7]), .A(A[7]), .B(xor_1_out[7]), .Cin(add_1bit_7_cout));  // open: Cout
  // Probe on R
  Overflow_detector overflow_detector_1 (
    .Sign_of_A(A[7]), .Result_sign(R[7]), .in_1(not_1_out), .Sign_of_B(B[7]), .out_5(Overflow));
  assign not_2_out = ~R;  // NOT_Gate not_2, 8 bits wide
  and and_1 (and_1_out, not_2_out[0], not_2_out[1], not_2_out[2], not_2_out[3], not_2_out[4], not_2_out[5], not_2_out[6], not_2_out[7]);
  and and_2 (Zero, and_1_out, ~Overflow);  // AND_Gate
endmodule

module Add_1Bit (
  input  A,
  input  B,
  input  Cin,
  output Sum,
  output Cout
);

  wire and_1_out, and_2_out, and_3_out, xor_1_out;

  xor xor_1 (xor_1_out, A, B);
  and and_1 (and_1_out, A, B);
  and and_2 (and_2_out, A, Cin);
  and and_3 (and_3_out, B, Cin);
  xor xor_2 (Sum, xor_1_out, Cin);
  or or_1 (Cout, and_1_out, and_2_out, and_3_out);

  // Notes on the sheet:
  //   Matthew Fong 260499247
  //   MAKE SURE THAT YOU OPENED THIS PROJECT IN "LOGISIM-EVOLUTION"
  //   YOU CAN FIND "LOGISIM-EVOLUTION" PRORAM IN THE ASSIGNMENT'S FOLDER
  //   DO NOT USE "LOGISIM" VERSION TO SOLVE THIS ASSIGNMENT!
endmodule

module Overflow_detector (
  input  in_1,
  input  Result_sign,
  input  Sign_of_A,
  input  Sign_of_B,
  output out_5
);

  wire and_1_out, and_2_out, and_3_out, and_4_out;

  and and_1 (and_1_out, ~Sign_of_A, ~Sign_of_B, Result_sign, ~in_1);  // AND_Gate
  and and_2 (and_2_out, Sign_of_A, Sign_of_B, ~Result_sign, ~in_1);  // AND_Gate
  and and_3 (and_3_out, Sign_of_A, ~Sign_of_B, ~Result_sign, in_1);  // AND_Gate
  and and_4 (and_4_out, ~Sign_of_A, Sign_of_B, Result_sign, in_1);  // AND_Gate
  or or_1 (out_5, and_1_out, and_2_out, and_3_out, and_4_out);

  // Notes on the sheet:
  //   Matthew Fong 260499247
  //   Add/ sub mode
  //   1 is sub/ 0 is add
  //   (+) + (+) = (-)
  //   (-) + (-) =(+)
  //   (-) - (+) = (+)
  //   (+) - (-) = (-)
endmodule

module ALU (
  input  [1:0] in_1,
  input  [7:0] in_2,
  input  [7:0] in_3,
  output [7:0] out_4,
  output out_5,
  output out_6
);

  wire and_1_out, decoder_1_out0, decoder_1_out1, decoder_1_out2, decoder_1_out3, or_1_out;
  wire [7:0] add_sub_8bits_1_r, twoscomplement_1_out_2;

  Decoder #(.select(2)) decoder_1 (
    .out0(decoder_1_out0), .out1(decoder_1_out1), .out2(decoder_1_out2), .out3(decoder_1_out3), .sel(in_1));  // open: en
  TwosComplement twoscomplement_1 (.in_1(in_3), .out_2(twoscomplement_1_out_2));
  and and_1 (and_1_out, decoder_1_out3, decoder_1_out2, decoder_1_out1);
  or or_1 (or_1_out, and_1_out, decoder_1_out0);
  Add_Sub_8Bits add_sub_8bits_1 (
    .Add_Sub(or_1_out), .A(in_2), .B(twoscomplement_1_out_2), .R(add_sub_8bits_1_r), .Zero(out_5),
    .Overflow(out_6));
  TwosComplement twoscomplement_2 (.in_1(add_sub_8bits_1_r), .out_2(out_4));

  // Notes on the sheet:
  //   0 0 - Add
  //   0 1 -Sub
  //   1 0 -BEQ
  //   1 1 -BNQ
  //   Sub Operations
  //   Add operation
endmodule

module ADD3IF5 (
  input  in_1,
  input  in_2,
  input  in_3,
  input  LSB,
  output out_5,
  output out_6,
  output out_7,
  output out_8
);

  wire add_1bit_1_cout, add_1bit_2_cout, add_1bit_3_cout, Five_out, not_1_out, or_1_out, Six_out, Svn_out;
  wire [3:0] add_1bit_1_sum;

  and Five (Five_out, in_2, ~in_3, LSB);  // AND_Gate
  and Six (Six_out, in_2, in_3, ~LSB);  // AND_Gate
  or or_1 (or_1_out, Five_out, Six_out, Svn_out, in_1);
  and Svn (Svn_out, in_2, in_3, LSB);
  Add_1Bit add_1bit_1 (.Sum(add_1bit_1_sum[0]), .A(LSB), .B(1'b1), .Cout(add_1bit_1_cout));  // open: Cin
  Add_1Bit add_1bit_2 (.Sum(add_1bit_1_sum[1]), .A(in_3), .B(1'b1), .Cout(add_1bit_2_cout), .Cin(add_1bit_1_cout));
  Add_1Bit add_1bit_3 (.Sum(add_1bit_1_sum[2]), .A(in_2), .B(1'b0), .Cout(add_1bit_3_cout), .Cin(add_1bit_2_cout));
  Add_1Bit add_1bit_4 (.Sum(add_1bit_1_sum[3]), .A(in_1), .B(1'b0), .Cin(add_1bit_3_cout));  // open: Cout
  // Probe on {in_1, in_2, in_3, LSB}
  assign {out_5, out_6, out_7, out_8} = not_1_out ? {in_1, in_2, in_3, LSB} : 4'bz;  // Controlled_Buffer controlled_buffer_1
  not not_1 (not_1_out, or_1_out);
  assign {out_5, out_6, out_7, out_8} = or_1_out ? add_1bit_1_sum : 4'bz;  // Controlled_Buffer controlled_buffer_2
  // Probe on {out_5, out_6, out_7, out_8}

  // Notes on the sheet:
  //   MSB
  //   5 or more
endmodule

module BCD_Convert (
  input  [7:0] in_1,
  output [3:0] out_2,
  output [3:0] out_3,
  output [3:0] out_4
);

  wire add3if5_1_out_5, add3if5_1_out_6, add3if5_1_out_7, add3if5_1_out_8, add3if5_2_out_5, add3if5_2_out_6,
       add3if5_2_out_7, add3if5_2_out_8, add3if5_3_out_5, add3if5_3_out_6, add3if5_3_out_7, add3if5_3_out_8,
       add3if5_4_out_6, add3if5_4_out_7, add3if5_4_out_8, add3if5_5_out_5, add3if5_5_out_6, add3if5_5_out_7,
       add3if5_5_out_8;

  // Probe on in_1
  ADD3IF5 add3if5_1 (
    .out_7(add3if5_1_out_7), .out_6(add3if5_1_out_6), .out_5(add3if5_1_out_5), .LSB(in_1[5]), .in_3(in_1[6]),
    .in_2(in_1[7]), .in_1(1'b0), .out_8(add3if5_1_out_8));
  ADD3IF5 add3if5_2 (
    .out_7(add3if5_2_out_7), .out_6(add3if5_2_out_6), .out_5(add3if5_2_out_5), .LSB(in_1[4]),
    .in_3(add3if5_1_out_8), .in_2(add3if5_1_out_7), .in_1(add3if5_1_out_6), .out_8(add3if5_2_out_8));
  ADD3IF5 add3if5_3 (
    .out_7(add3if5_3_out_7), .out_6(add3if5_3_out_6), .out_5(add3if5_3_out_5), .LSB(in_1[3]),
    .in_3(add3if5_2_out_8), .in_2(add3if5_2_out_7), .in_1(add3if5_2_out_6), .out_8(add3if5_3_out_8));
  ADD3IF5 add3if5_4 (
    .out_7(add3if5_4_out_7), .out_6(add3if5_4_out_6), .out_5(out_2[1]), .LSB(add3if5_3_out_5),
    .in_3(add3if5_2_out_5), .in_2(add3if5_1_out_5), .in_1(1'b0), .out_8(add3if5_4_out_8));
  ADD3IF5 add3if5_5 (
    .out_7(add3if5_5_out_7), .out_6(add3if5_5_out_6), .out_5(add3if5_5_out_5), .LSB(in_1[2]),
    .in_3(add3if5_3_out_8), .in_2(add3if5_3_out_7), .in_1(add3if5_3_out_6), .out_8(add3if5_5_out_8));
  ADD3IF5 add3if5_6 (
    .out_7(out_3[2]), .out_6(out_3[3]), .out_5(out_2[0]), .LSB(add3if5_5_out_5), .in_3(add3if5_4_out_8),
    .in_2(add3if5_4_out_7), .in_1(add3if5_4_out_6), .out_8(out_3[1]));
  ADD3IF5 add3if5_7 (
    .out_7(out_4[2]), .out_6(out_4[3]), .out_5(out_3[0]), .LSB(in_1[1]), .in_3(add3if5_5_out_8),
    .in_2(add3if5_5_out_7), .in_1(add3if5_5_out_6), .out_8(out_4[1]));
  // Probe on {out_4[3:1], in_1[0]}
  // Probe on {2'b00, out_2[1:0]}
  // Probe on out_3

  assign out_2[3:2] = 2'b00;
  assign out_4[0] = in_1[0];
endmodule

module Register_4b (
  input  Address_Bit,
  input  Clock,
  input  [3:0] in_3,
  input  R_Mode,
  input  in_5,
  output [3:0] out_6,
  output [3:0] out_7
);

  wire and_1_out, and_2_out, and_3_out, and_4_out, and_5_out, and_6_out, and_7_out, and_8_out;

  and and_1 (and_1_out, in_3[0], R_Mode, Address_Bit);
  and and_2 (and_2_out, ~in_3[0], R_Mode, Address_Bit);  // AND_Gate
  and and_3 (and_3_out, in_3[1], R_Mode, Address_Bit);
  and and_4 (and_4_out, ~in_3[1], R_Mode, Address_Bit);  // AND_Gate
  and and_5 (and_5_out, in_3[2], R_Mode, Address_Bit);
  and and_6 (and_6_out, ~in_3[2], R_Mode, Address_Bit);  // AND_Gate
  and and_7 (and_7_out, in_3[3], R_Mode, Address_Bit);
  and and_8 (and_8_out, ~in_3[3], R_Mode, Address_Bit);  // AND_Gate
  S_R_Flip_Flop s_r_ff_1 (.S(and_1_out), .R(and_2_out), .clk(Clock), .Q(out_6[0]), .reset(in_5));  // open: Qn, preset
  S_R_Flip_Flop s_r_ff_2 (.S(and_3_out), .R(and_4_out), .clk(Clock), .Q(out_6[1]), .reset(in_5));  // open: Qn, preset
  S_R_Flip_Flop s_r_ff_3 (.S(and_5_out), .R(and_6_out), .clk(Clock), .Q(out_6[2]), .reset(in_5));  // open: Qn, preset
  S_R_Flip_Flop s_r_ff_4 (.S(and_7_out), .R(and_8_out), .clk(Clock), .Q(out_6[3]), .reset(in_5));  // open: Qn, preset

  assign out_7 = out_6;

  // Notes on the sheet:
  //   CLR
endmodule

module DPath_FETCH (
  input  [3:0] in_1,
  output [1:0] out_2,
  output [1:0] out_3,
  output [1:0] out_4,
  output [1:0] out_5,
  output [1:0] out_6,
  output [1:0] out_7,
  output [1:0] out_8,
  output [1:0] out_9
);

  wire decoder_1_out0, decoder_1_out1, decoder_1_out2, decoder_1_out3, decoder_1_out4;

  Decoder #(.select(4)) decoder_1 (
    .out0(decoder_1_out0), .out1(decoder_1_out1), .out2(decoder_1_out2), .out3(decoder_1_out3),
    .out4(decoder_1_out4), .sel(in_1));  // open: out5, out6, out7, out8, out9, out10, out11, out12, out13, out14, out15, en
  or or_1 (out_2[1], decoder_1_out0, decoder_1_out1);
  or or_2 (out_2[0], 1'b0, decoder_1_out1);
  or or_3 (out_4[1], decoder_1_out0, decoder_1_out1);
  buf or_4 (out_4[0], decoder_1_out0);  // OR_Gate
  or or_5 (out_5[1], decoder_1_out1, decoder_1_out2);
  buf or_6 (out_5[0], decoder_1_out1);  // OR_Gate
  buf or_7 (out_6[1], decoder_1_out2);  // OR_Gate
  buf or_8 (out_6[0], 1'b0);  // OR_Gate
  or or_9 (out_7[1], decoder_1_out2, decoder_1_out3);
  buf or_10 (out_7[0], decoder_1_out2);  // OR_Gate
  or or_11 (out_8[1], decoder_1_out3, decoder_1_out4);
  buf or_12 (out_8[0], decoder_1_out3);  // OR_Gate
  buf or_13 (out_9[1], decoder_1_out4);  // OR_Gate
  buf or_14 (out_9[0], decoder_1_out4);  // OR_Gate
  // Probe on out_2
  // Probe on out_4
  // Probe on out_5
  // Probe on out_6
  // Probe on out_7
  // Probe on out_8
  // Probe on out_9
  or or_15 (out_3[1], decoder_1_out0, decoder_1_out1);
  buf or_16 (out_3[0], decoder_1_out0);  // OR_Gate
  // Probe on out_3

  // Notes on the sheet:
  //   PC
  //   RAM
  //   MAR
  //   RA
  //   RD
  //   MBR
  //   IR
  //   PC Count
endmodule

module PHASECLOCK (
  input  in_1,
  input  Reset,
  output [3:0] out_3,
  output [3:0] out_4
);

  wire and_1_out, and_2_out, and_3_out, or_1_out;

  J_K_Flip_Flop j_k_ff_1 (.J(1'b1), .K(1'b1), .clk(in_1), .Q(out_3[0]), .reset(or_1_out));  // open: Qn, preset
  J_K_Flip_Flop j_k_ff_2 (.J(out_3[0]), .K(out_3[0]), .clk(in_1), .Q(out_3[1]), .reset(or_1_out));  // open: Qn, preset
  // Probe on out_3
  and and_1 (and_1_out, out_3[0], out_3[1]);
  J_K_Flip_Flop j_k_ff_3 (
    .J(and_1_out), .K(and_1_out), .clk(in_1), .Q(out_3[2]), .reset(or_1_out));  // open: Qn, preset
  and and_2 (and_2_out, and_1_out, out_3[2]);
  J_K_Flip_Flop j_k_ff_4 (
    .J(and_2_out), .K(and_2_out), .clk(in_1), .Q(out_3[3]), .reset(or_1_out));  // open: Qn, preset
  and and_3 (and_3_out, out_3[0], out_3[1], ~out_3[2], out_3[3]);  // AND_Gate
  or or_1 (or_1_out, and_3_out, Reset);

  assign out_4 = out_3;
endmodule

module Register_8b_passthrough (
  input  Address_Bit,
  input  Clock,
  input  [7:0] in_3,
  input  R_W_Mode,
  input  CLEAR,
  output [7:0] out_6,
  output [7:0] out_7
);

  wire and_1_out, and_2_out, and_3_out, and_4_out, and_5_out, and_6_out, and_7_out, and_8_out, and_9_out,
       and_10_out, and_11_out, and_12_out, and_13_out, and_14_out, and_15_out, and_16_out, and_17_out,
       controlled_buffer_1_out, controlled_buffer_2_out, controlled_buffer_3_out, controlled_buffer_4_out,
       controlled_buffer_5_out, controlled_buffer_6_out, controlled_buffer_7_out, controlled_buffer_8_out,
       not_1_out;

  assign controlled_buffer_1_out = and_1_out ? in_3[0] : 1'bz;  // Controlled_Buffer controlled_buffer_1
  assign controlled_buffer_2_out = and_1_out ? in_3[1] : 1'bz;  // Controlled_Buffer controlled_buffer_2
  assign controlled_buffer_3_out = and_1_out ? in_3[2] : 1'bz;  // Controlled_Buffer controlled_buffer_3
  assign controlled_buffer_4_out = and_1_out ? in_3[3] : 1'bz;  // Controlled_Buffer controlled_buffer_4
  assign controlled_buffer_5_out = and_1_out ? in_3[4] : 1'bz;  // Controlled_Buffer controlled_buffer_5
  assign controlled_buffer_6_out = and_1_out ? in_3[5] : 1'bz;  // Controlled_Buffer controlled_buffer_6
  assign controlled_buffer_7_out = and_1_out ? in_3[6] : 1'bz;  // Controlled_Buffer controlled_buffer_7
  assign controlled_buffer_8_out = and_1_out ? in_3[7] : 1'bz;  // Controlled_Buffer controlled_buffer_8
  and and_1 (and_1_out, Address_Bit, R_W_Mode);
  and and_2 (and_2_out, controlled_buffer_1_out, R_W_Mode, 1'b1);
  and and_3 (and_3_out, ~controlled_buffer_1_out, R_W_Mode, 1'b1);  // AND_Gate
  and and_4 (and_4_out, controlled_buffer_2_out, R_W_Mode, 1'b1);
  and and_5 (and_5_out, ~controlled_buffer_2_out, R_W_Mode, 1'b1);  // AND_Gate
  and and_6 (and_6_out, controlled_buffer_3_out, R_W_Mode, 1'b1);
  and and_7 (and_7_out, ~controlled_buffer_3_out, R_W_Mode, 1'b1);  // AND_Gate
  and and_8 (and_8_out, controlled_buffer_4_out, R_W_Mode, 1'b1);
  and and_9 (and_9_out, ~controlled_buffer_4_out, R_W_Mode, 1'b1);  // AND_Gate
  and and_10 (and_10_out, controlled_buffer_5_out, R_W_Mode, 1'b1);
  and and_11 (and_11_out, ~controlled_buffer_5_out, R_W_Mode, 1'b1);  // AND_Gate
  and and_12 (and_12_out, controlled_buffer_6_out, R_W_Mode, 1'b1);
  and and_13 (and_13_out, ~controlled_buffer_6_out, R_W_Mode, 1'b1);  // AND_Gate
  and and_14 (and_14_out, controlled_buffer_7_out, R_W_Mode, 1'b1);
  and and_15 (and_15_out, ~controlled_buffer_7_out, R_W_Mode, 1'b1);  // AND_Gate
  and and_16 (and_16_out, controlled_buffer_8_out, R_W_Mode, 1'b1);
  and and_17 (and_17_out, ~controlled_buffer_8_out, R_W_Mode, 1'b1);  // AND_Gate
  S_R_Flip_Flop s_r_ff_1 (.S(and_2_out), .R(and_3_out), .clk(Clock), .Q(out_6[0]), .reset(CLEAR));  // open: Qn, preset
  S_R_Flip_Flop s_r_ff_2 (.S(and_4_out), .R(and_5_out), .clk(Clock), .Q(out_6[1]), .reset(CLEAR));  // open: Qn, preset
  S_R_Flip_Flop s_r_ff_3 (.S(and_6_out), .R(and_7_out), .clk(Clock), .Q(out_6[2]), .reset(CLEAR));  // open: Qn, preset
  S_R_Flip_Flop s_r_ff_4 (.S(and_8_out), .R(and_9_out), .clk(Clock), .Q(out_6[3]), .reset(CLEAR));  // open: Qn, preset
  S_R_Flip_Flop s_r_ff_5 (
    .S(and_10_out), .R(and_11_out), .clk(Clock), .Q(out_6[4]), .reset(CLEAR));  // open: Qn, preset
  S_R_Flip_Flop s_r_ff_6 (
    .S(and_12_out), .R(and_13_out), .clk(Clock), .Q(out_6[5]), .reset(CLEAR));  // open: Qn, preset
  S_R_Flip_Flop s_r_ff_7 (
    .S(and_14_out), .R(and_15_out), .clk(Clock), .Q(out_6[6]), .reset(CLEAR));  // open: Qn, preset
  S_R_Flip_Flop s_r_ff_8 (
    .S(and_16_out), .R(and_17_out), .clk(Clock), .Q(out_6[7]), .reset(CLEAR));  // open: Qn, preset
  not not_1 (not_1_out, R_W_Mode);
  and and_18 (out_7[0], out_6[0], not_1_out);
  and and_19 (out_7[1], out_6[1], not_1_out);
  and and_20 (out_7[2], out_6[2], not_1_out);
  and and_21 (out_7[3], out_6[3], not_1_out);
  and and_22 (out_7[4], out_6[4], not_1_out);
  and and_23 (out_7[5], out_6[5], not_1_out);
  and and_24 (out_7[6], out_6[6], not_1_out);
  and and_25 (out_7[7], out_6[7], not_1_out);

  // Notes on the sheet:
  //   Probe
endmodule

module DPath_LOADSTORE (
  input  [7:0] in_1,
  input  [3:0] in_2,
  output [7:0] Address_out,
  output [1:0] out_4,
  output [1:0] out_5,
  output [1:0] out_6,
  output [1:0] out_7,
  output [1:0] out_8,
  output Reset
);

  wire and_1_out, and_2_out, and_3_out, and_4_out, and_5_out, and_6_out, and_7_out, and_8_out, and_9_out,
       and_10_out, and_11_out, and_12_out, decoder_1_out5, decoder_1_out6, decoder_1_out7, decoder_1_out8,
       decoder_2_out5, decoder_2_out6, decoder_2_out7, decoder_2_out8, LOAD_out, or_2_out, r0, r1, STORE_out;
  wire [7:0] bit_extender_1_out;

  and STORE (STORE_out, ~in_1[7], in_1[6], in_1[5]);  // AND_Gate
  buf u_r1 (r1, in_1[0]);  // AND_Gate
  buf u_r0 (r0, ~in_1[0]);  // AND_Gate AND_Gate
  and LOAD (LOAD_out, ~in_1[5], in_1[6], ~in_1[7]);  // AND_Gate
  Decoder #(.select(4)) decoder_1 (
    .out5(decoder_1_out5), .out6(decoder_1_out6), .out7(decoder_1_out7), .out8(decoder_1_out8), .sel(in_2));  // open: out0, out1, out2, out3, out4, out9, out10, out11, out12, out13, out14, out15, en
  Decoder #(.select(4)) decoder_2 (
    .out5(decoder_2_out5), .out6(decoder_2_out6), .out7(decoder_2_out7), .out8(decoder_2_out8), .sel(in_2));  // open: out0, out1, out2, out3, out4, out9, out10, out11, out12, out13, out14, out15, en
  and and_1 (and_1_out, decoder_2_out8, STORE_out);
  and and_2 (and_2_out, decoder_1_out8, LOAD_out);
  or or_1 (Reset, and_1_out, and_2_out);
  // Probe on in_1[4:1]
  and and_3 (and_3_out, decoder_1_out5, LOAD_out);
  and and_4 (and_4_out, decoder_1_out6, LOAD_out);
  and and_5 (and_5_out, decoder_1_out7, LOAD_out);
  and and_6 (and_6_out, decoder_2_out5, STORE_out);
  and and_7 (and_7_out, decoder_2_out6, STORE_out);
  and and_8 (and_8_out, decoder_2_out7, STORE_out);
  assign bit_extender_1_out = {{4{1'b0}}, in_1[4:1]};  // Bit_Extender bit_extender_1
  and and_9 (and_9_out, and_5_out, r0);
  and and_10 (and_10_out, and_7_out, r0);
  and and_11 (and_11_out, and_5_out, r1);
  and and_12 (and_12_out, and_7_out, r1);
  assign Address_out = or_2_out ? bit_extender_1_out : 8'bz;  // Controlled_Buffer controlled_buffer_1
  or or_2 (or_2_out, and_3_out, and_6_out);
  or or_3 (out_4[1], and_8_out, and_4_out, and_5_out, and_7_out);
  or or_4 (out_4[0], and_4_out, and_7_out);
  or or_5 (out_5[1], and_8_out, and_3_out, and_6_out, and_4_out);
  or or_6 (out_5[0], and_3_out, and_6_out);
  or or_7 (out_6[1], and_4_out, and_8_out);
  buf or_8 (out_6[0], and_8_out);  // OR_Gate
  or or_9 (out_7[1], and_9_out, and_10_out);
  buf or_10 (out_7[0], and_9_out);  // OR_Gate
  or or_11 (out_8[1], and_11_out, and_12_out);
  buf or_12 (out_8[0], and_11_out);  // OR_Gate
  // Probe on out_4
  // Probe on out_5
  // Probe on out_6
  // Probe on out_7
  // Probe on out_8

  // Notes on the sheet:
  //   RD
  //   On
  //   R
  //   RA
  //   On
  //   R
  //   RAM
  //   On
  //   R
  //   $R0
  //   On
  //   R
  //   $r1
  //   On
  //   R
endmodule

module CONTROLUNIT (
  input  [7:0] in_1,
  input  [3:0] in_2,
  input  in_3,
  output [7:0] out_4,
  output [1:0] out_5,
  output [1:0] out_6,
  output READ,
  output [1:0] out_8,
  output PRINT,
  output [1:0] out_10,
  output [1:0] out_11,
  output [1:0] out_12,
  output [1:0] out_13,
  output [1:0] out_14,
  output [1:0] out_15,
  output [1:0] out_16,
  output STOP,
  output RESET
);

  wire dpath_addsub_1_out_9, dpath_branch_1_out_11, dpath_loadstore_1_reset, dpath_printread_1_reset,
       dpath_stop_1_out_3;
  wire [1:0] dpath_addsub_1_out_3, dpath_addsub_1_out_4, dpath_addsub_1_out_5, dpath_addsub_1_out_6,
       dpath_addsub_1_out_7, dpath_addsub_1_out_8, dpath_branch_1_out_5, dpath_branch_1_out_6,
       dpath_branch_1_out_7, dpath_branch_1_out_8, dpath_branch_1_out_9, dpath_loadstore_1_out_4,
       dpath_loadstore_1_out_5, dpath_loadstore_1_out_6, dpath_loadstore_1_out_7, dpath_loadstore_1_out_8,
       dpath_printread_1_out_5, dpath_printread_1_out_6;

  or or_1 (RESET, dpath_loadstore_1_reset, dpath_branch_1_out_11, dpath_printread_1_reset, dpath_addsub_1_out_9);
  DPath_PRINTREAD dpath_printread_1 (
    .in_1(in_1), .out_3(READ), .out_4(PRINT), .in_2(in_2), .out_5(dpath_printread_1_out_5),
    .out_6(dpath_printread_1_out_6), .Reset(dpath_printread_1_reset));
  DPath_ADDSUB dpath_addsub_1 (
    .out_6(dpath_addsub_1_out_6), .in_2(in_2), .out_7(dpath_addsub_1_out_7), .in_1(in_1),
    .out_5(dpath_addsub_1_out_5), .out_3(dpath_addsub_1_out_3), .out_9(dpath_addsub_1_out_9),
    .out_8(dpath_addsub_1_out_8), .out_4(dpath_addsub_1_out_4));
  DPath_STOP dpath_stop_1 (.out_3(dpath_stop_1_out_3), .in_1(in_1), .in_2(in_2));
  DPath_BRANCH dpath_branch_1 (
    .out_9(dpath_branch_1_out_9), .out_8(dpath_branch_1_out_8), .out_7(dpath_branch_1_out_7),
    .out_6(dpath_branch_1_out_6), .out_5(dpath_branch_1_out_5), .out_4(out_4), .ALU_ZERO(in_3), .in_2(in_2),
    .in_1(in_1), .out_10(out_15), .out_11(dpath_branch_1_out_11));
  DPath_LOADSTORE dpath_loadstore_1 (
    .out_5(dpath_loadstore_1_out_5), .out_6(dpath_loadstore_1_out_6), .out_4(dpath_loadstore_1_out_4),
    .out_8(dpath_loadstore_1_out_8), .in_2(in_2), .out_7(dpath_loadstore_1_out_7), .Address_out(out_4),
    .in_1(in_1), .Reset(dpath_loadstore_1_reset));
  assign out_5 = dpath_loadstore_1_out_4;  // OR_Gate RD, 2 bits wide OR_Gate
  assign out_6 = dpath_loadstore_1_out_5;  // OR_Gate RA, 2 bits wide OR_Gate
  assign out_8 = dpath_loadstore_1_out_6;  // OR_Gate RAM, 2 bits wide OR_Gate
  assign out_10 = dpath_addsub_1_out_7 | dpath_printread_1_out_5 | dpath_branch_1_out_8 | dpath_loadstore_1_out_7;  // OR_Gate S0, 2 bits wide
  assign out_11 = dpath_addsub_1_out_8 | dpath_printread_1_out_6 | dpath_branch_1_out_9 | dpath_loadstore_1_out_8;  // OR_Gate S1, 2 bits wide
  assign out_13 = dpath_addsub_1_out_4 | dpath_branch_1_out_6;  // OR_Gate L, 2 bits wide
  assign out_14 = dpath_addsub_1_out_5 | dpath_branch_1_out_7;  // OR_Gate R, 2 bits wide
  assign out_16 = dpath_addsub_1_out_6;  // OR_Gate A, 2 bits wide OR_Gate
  assign out_12 = dpath_addsub_1_out_3 | dpath_branch_1_out_5;  // OR_Gate ALUOP, 2 bits wide
  buf u_STOP (STOP, dpath_stop_1_out_3);  // OR_Gate
endmodule

module INPUTROM (
  input  in_1,
  input  in_2,
  input  in_3,
  input  in_4,
  input  in_5,
  input  in_6,
  input  in_7,
  input  in_8,
  input  in_9,
  input  in_10,
  output [7:0] out_11
);

  or or_1 (out_11[0], in_8, in_6, in_10, in_2, in_4);
  or or_2 (out_11[1], in_8, in_7, in_3, in_4);
  or or_3 (out_11[2], in_8, in_7, in_6, in_5);
  or or_4 (out_11[3], in_9, in_10);

  assign out_11[7:4] = 4'b0000;
endmodule

module Register_8b_passin (
  input  Address_Bit,
  input  Clock,
  input  [7:0] in_3,
  input  in_4,
  output [7:0] out_5,
  output [7:0] out_6
);

  wire and_1_out, and_2_out, and_3_out, and_4_out, and_5_out, and_6_out, and_7_out, and_8_out, and_9_out,
       and_10_out, and_11_out, and_12_out, and_13_out, and_14_out, and_15_out, and_16_out, and_17_out,
       and_18_out, and_19_out, and_20_out, and_21_out, and_22_out, and_23_out, and_24_out, and_25_out,
       controlled_buffer_1_out, controlled_buffer_2_out, controlled_buffer_3_out, controlled_buffer_4_out,
       controlled_buffer_5_out, controlled_buffer_6_out, controlled_buffer_7_out, controlled_buffer_8_out;

  assign controlled_buffer_1_out = 1'b1 ? in_3[0] : 1'bz;  // Controlled_Buffer controlled_buffer_1
  assign controlled_buffer_2_out = 1'b1 ? in_3[1] : 1'bz;  // Controlled_Buffer controlled_buffer_2
  assign controlled_buffer_3_out = 1'b1 ? in_3[2] : 1'bz;  // Controlled_Buffer controlled_buffer_3
  assign controlled_buffer_4_out = 1'b1 ? in_3[3] : 1'bz;  // Controlled_Buffer controlled_buffer_4
  assign controlled_buffer_5_out = 1'b1 ? in_3[4] : 1'bz;  // Controlled_Buffer controlled_buffer_5
  assign controlled_buffer_6_out = 1'b1 ? in_3[5] : 1'bz;  // Controlled_Buffer controlled_buffer_6
  assign controlled_buffer_7_out = 1'b1 ? in_3[6] : 1'bz;  // Controlled_Buffer controlled_buffer_7
  assign controlled_buffer_8_out = 1'b1 ? in_3[7] : 1'bz;  // Controlled_Buffer controlled_buffer_8
  and and_1 (and_1_out, controlled_buffer_1_out, 1'b1);
  and and_2 (and_2_out, ~controlled_buffer_1_out, 1'b1);  // AND_Gate
  and and_3 (and_3_out, controlled_buffer_2_out, 1'b1);
  and and_4 (and_4_out, ~controlled_buffer_2_out, 1'b1);  // AND_Gate
  and and_5 (and_5_out, controlled_buffer_3_out, 1'b1);
  and and_6 (and_6_out, ~controlled_buffer_3_out, 1'b1);  // AND_Gate
  and and_7 (and_7_out, controlled_buffer_4_out, 1'b1);
  and and_8 (and_8_out, ~controlled_buffer_4_out, 1'b1);  // AND_Gate
  and and_9 (and_9_out, controlled_buffer_5_out, 1'b1);
  and and_10 (and_10_out, ~controlled_buffer_5_out, 1'b1);  // AND_Gate
  and and_11 (and_11_out, controlled_buffer_6_out, 1'b1);
  and and_12 (and_12_out, ~controlled_buffer_6_out, 1'b1);  // AND_Gate
  and and_13 (and_13_out, controlled_buffer_7_out, 1'b1);
  and and_14 (and_14_out, ~controlled_buffer_7_out, 1'b1);  // AND_Gate
  and and_15 (and_15_out, controlled_buffer_8_out, 1'b1);
  and and_16 (and_16_out, ~controlled_buffer_8_out, 1'b1);  // AND_Gate
  S_R_Flip_Flop s_r_ff_1 (.S(and_1_out), .R(and_2_out), .clk(Clock), .Q(out_5[0]), .reset(in_4));  // open: Qn, preset
  S_R_Flip_Flop s_r_ff_2 (.S(and_3_out), .R(and_4_out), .clk(Clock), .Q(out_5[1]), .reset(in_4));  // open: Qn, preset
  S_R_Flip_Flop s_r_ff_3 (.S(and_5_out), .R(and_6_out), .clk(Clock), .Q(out_5[2]), .reset(in_4));  // open: Qn, preset
  S_R_Flip_Flop s_r_ff_4 (.S(and_7_out), .R(and_8_out), .clk(Clock), .Q(out_5[3]), .reset(in_4));  // open: Qn, preset
  S_R_Flip_Flop s_r_ff_5 (.S(and_9_out), .R(and_10_out), .clk(Clock), .Q(out_5[4]), .reset(in_4));  // open: Qn, preset
  S_R_Flip_Flop s_r_ff_6 (.S(and_11_out), .R(and_12_out), .clk(Clock), .Q(out_5[5]), .reset(in_4));  // open: Qn, preset
  S_R_Flip_Flop s_r_ff_7 (.S(and_13_out), .R(and_14_out), .clk(Clock), .Q(out_5[6]), .reset(in_4));  // open: Qn, preset
  S_R_Flip_Flop s_r_ff_8 (.S(and_15_out), .R(and_16_out), .clk(Clock), .Q(out_5[7]), .reset(in_4));  // open: Qn, preset
  assign out_6[0] = and_25_out ? and_17_out : 1'bz;  // Controlled_Buffer controlled_buffer_9
  and and_17 (and_17_out, out_5[0], Address_Bit);
  and and_18 (and_18_out, out_5[1], Address_Bit);
  assign out_6[1] = and_25_out ? and_18_out : 1'bz;  // Controlled_Buffer controlled_buffer_10
  and and_19 (and_19_out, out_5[2], Address_Bit);
  assign out_6[2] = and_25_out ? and_19_out : 1'bz;  // Controlled_Buffer controlled_buffer_11
  and and_20 (and_20_out, out_5[3], Address_Bit);
  assign out_6[3] = and_25_out ? and_20_out : 1'bz;  // Controlled_Buffer controlled_buffer_12
  and and_21 (and_21_out, out_5[4], Address_Bit);
  assign out_6[4] = and_25_out ? and_21_out : 1'bz;  // Controlled_Buffer controlled_buffer_13
  and and_22 (and_22_out, out_5[5], Address_Bit);
  assign out_6[5] = and_25_out ? and_22_out : 1'bz;  // Controlled_Buffer controlled_buffer_14
  and and_23 (and_23_out, out_5[6], Address_Bit);
  assign out_6[6] = and_25_out ? and_23_out : 1'bz;  // Controlled_Buffer controlled_buffer_15
  and and_24 (and_24_out, out_5[7], Address_Bit);
  assign out_6[7] = and_25_out ? and_24_out : 1'bz;  // Controlled_Buffer controlled_buffer_16
  buf and_25 (and_25_out, Address_Bit);  // AND_Gate

  // Notes on the sheet:
  //   CLEAR
  //   Probe
endmodule

module DPath_PRINTREAD (
  input  [7:0] in_1,
  input  [3:0] in_2,
  output out_3,
  output out_4,
  output [1:0] out_5,
  output [1:0] out_6,
  output Reset
);

  wire a, and_1_out, and_2_out, and_3_out, and_4_out, and_5_out, and_6_out, and_7_out, and_8_out, b,
       decoder_1_out5, decoder_1_out6, decoder_2_out5, decoder_2_out6, print_out, read_out;

  and print (print_out, ~in_1[7], ~in_1[6], ~in_1[5], ~in_1[4], in_1[3], in_1[2]);  // AND_Gate
  buf so (a, ~in_1[0]);  // AND_Gate AND_Gate
  buf s1 (b, in_1[0]);  // AND_Gate
  and read (read_out, ~in_1[7], ~in_1[6], ~in_1[5], ~in_1[4], in_1[3], ~in_1[2]);  // AND_Gate
  Decoder #(.select(4)) decoder_1 (
    .out5(decoder_1_out5), .out6(decoder_1_out6), .sel(in_2));  // open: out0, out1, out2, out3, out4, out7, out8, out9, out10, out11, out12, out13, out14, out15, en
  Decoder #(.select(4)) decoder_2 (
    .out5(decoder_2_out5), .out6(decoder_2_out6), .sel(in_2));  // open: out0, out1, out2, out3, out4, out7, out8, out9, out10, out11, out12, out13, out14, out15, en
  and and_1 (and_1_out, decoder_2_out6, print_out);
  and and_2 (and_2_out, decoder_1_out6, read_out);
  or or_1 (Reset, and_1_out, and_2_out);
  and and_3 (and_3_out, decoder_1_out5, read_out);
  and and_4 (and_4_out, decoder_2_out5, print_out);
  and and_5 (and_5_out, and_3_out, a);
  and and_6 (and_6_out, and_4_out, a);
  and and_7 (and_7_out, and_3_out, b);
  and and_8 (and_8_out, and_4_out, b);
  or or_2 (out_3, and_3_out, and_3_out);
  buf or_3 (out_4, and_4_out);  // OR_Gate
  or or_4 (out_5[1], and_5_out, and_6_out);
  buf or_5 (out_5[0], and_5_out);  // OR_Gate
  or or_6 (out_6[1], and_7_out, and_8_out);
  buf or_7 (out_6[0], and_7_out);  // OR_Gate
  // Probe on out_3
  // Probe on out_4
  // Probe on out_5
  // Probe on out_6

  // Notes on the sheet:
  //   READ REG
  //   On
  //   PRINT REG
  //   On
  //   $r0
  //   On
  //   R
  //   $r1
  //   On
  //   R
endmodule

module TwosComplement (
  input  [7:0] in_1,
  output [7:0] out_2
);

  wire add_1bit_1_cout, add_1bit_2_cout, add_1bit_3_cout, add_1bit_4_cout, add_1bit_5_cout, add_1bit_6_cout,
       add_1bit_7_cout, not_1_out, not_2_out, not_3_out, not_4_out, not_5_out, not_6_out, not_7_out;
  wire [7:0] add_1bit_1_sum, and_2_out, and_3_out;
  wire [7:7] and_1_out;

  // Probe on in_1[6:0]
  not not_1 (not_1_out, in_1[0]);
  not not_2 (not_2_out, in_1[1]);
  not not_3 (not_3_out, in_1[2]);
  not not_4 (not_4_out, in_1[3]);
  not not_5 (not_5_out, in_1[4]);
  not not_6 (not_6_out, in_1[5]);
  not not_7 (not_7_out, in_1[6]);
  and and_1 (and_1_out[7], in_1[7], ~in_1[2], ~in_1[1], ~in_1[0]);  // AND_Gate
  Add_1Bit add_1bit_1 (.Sum(add_1bit_1_sum[0]), .A(not_1_out), .B(1'b0), .Cout(add_1bit_1_cout), .Cin(1'b1));
  Add_1Bit add_1bit_2 (.Sum(add_1bit_1_sum[1]), .A(not_2_out), .B(1'b0), .Cout(add_1bit_2_cout), .Cin(add_1bit_1_cout));
  Add_1Bit add_1bit_3 (.Sum(add_1bit_1_sum[2]), .A(not_3_out), .B(1'b0), .Cout(add_1bit_3_cout), .Cin(add_1bit_2_cout));
  Add_1Bit add_1bit_4 (.Sum(add_1bit_1_sum[3]), .A(not_4_out), .B(1'b0), .Cout(add_1bit_4_cout), .Cin(add_1bit_3_cout));
  Add_1Bit add_1bit_5 (.Sum(add_1bit_1_sum[4]), .A(not_5_out), .B(1'b0), .Cout(add_1bit_5_cout), .Cin(add_1bit_4_cout));
  Add_1Bit add_1bit_6 (.Sum(add_1bit_1_sum[5]), .A(not_6_out), .B(1'b0), .Cout(add_1bit_6_cout), .Cin(add_1bit_5_cout));
  Add_1Bit add_1bit_7 (.Sum(add_1bit_1_sum[6]), .A(not_7_out), .B(1'b0), .Cout(add_1bit_7_cout), .Cin(add_1bit_6_cout));
  Add_1Bit add_1bit_8 (.Sum(add_1bit_1_sum[7]), .A(1'b0), .B(1'b1), .Cin(add_1bit_7_cout));  // open: Cout
  assign and_2_out = in_1 & ~{8{in_1[7]}} & ~{8{and_1_out[7]}};  // AND_Gate and_2, 8 bits wide
  assign and_3_out = {8{in_1[7]}} & ~{8{and_1_out[7]}} & add_1bit_1_sum;  // AND_Gate and_3, 8 bits wide
  // Probe on out_2
  assign out_2 = and_2_out | and_3_out;  // OR_Gate or_1, 8 bits wide
endmodule

module DPath_ADDSUB (
  input  [7:0] in_1,
  input  [3:0] in_2,
  output [1:0] out_3,
  output [1:0] out_4,
  output [1:0] out_5,
  output [1:0] out_6,
  output [1:0] out_7,
  output [1:0] out_8,
  output out_9
);

  wire A, ADD_out, and_6_out, and_7_out, and_8_out, and_9_out, and_11_out, and_12_out, and_13_out,
       and_14_out, and_15_out, and_16_out, B, C, D, decoder_1_out5, decoder_1_out6, decoder_1_out7,
       decoder_1_out8, decoder_1_out9, or_1_out, SUB_out;

  and ADD (ADD_out, ~in_1[7], ~in_1[6], ~in_1[5], in_1[4], ~in_1[3]);  // AND_Gate
  buf and_1 (C, ~in_1[1]);  // AND_Gate AND_Gate
  buf and_2 (D, in_1[1]);  // AND_Gate
  and SUB (SUB_out, in_1[3], in_1[4], ~in_1[5], ~in_1[6], ~in_1[7]);  // AND_Gate
  buf and_3 (A, ~in_1[0]);  // AND_Gate AND_Gate
  Decoder #(.select(4)) decoder_1 (
    .out5(decoder_1_out5), .out6(decoder_1_out6), .out7(decoder_1_out7), .out8(decoder_1_out8),
    .out9(decoder_1_out9), .sel(in_2));  // open: out0, out1, out2, out3, out4, out10, out11, out12, out13, out14, out15, en
  buf and_4 (B, in_1[0]);  // AND_Gate
  or or_1 (or_1_out, SUB_out, ADD_out);
  and and_5 (out_9, decoder_1_out9, or_1_out);
  and and_6 (and_6_out, decoder_1_out5, or_1_out);
  and and_7 (and_7_out, decoder_1_out6, or_1_out);
  and and_8 (and_8_out, decoder_1_out7, or_1_out);
  and and_9 (and_9_out, decoder_1_out8, or_1_out);
  and and_10 (out_3[0], and_8_out, SUB_out);
  and and_11 (and_11_out, A, and_6_out);
  and and_12 (and_12_out, A, and_9_out);
  and and_13 (and_13_out, and_7_out, C);
  and and_14 (and_14_out, B, and_6_out);
  and and_15 (and_15_out, B, and_9_out);
  and and_16 (and_16_out, and_7_out, D);
  or or_2 (out_4[1], and_6_out, and_8_out);
  buf or_3 (out_4[0], and_6_out);  // OR_Gate
  or or_4 (out_5[1], and_7_out, and_8_out);
  buf or_5 (out_5[0], and_7_out);  // OR_Gate
  or or_6 (out_6[1], and_8_out, and_9_out);
  buf or_7 (out_6[0], and_8_out);  // OR_Gate
  or or_8 (out_7[1], and_11_out, and_13_out, and_12_out);
  buf or_9 (out_7[0], and_9_out);  // OR_Gate
  or or_10 (out_8[1], and_14_out, and_16_out, and_15_out);
  buf or_11 (out_8[0], and_9_out);  // OR_Gate
  // Probe on {1'b0, out_3[0]}
  // Probe on out_4
  // Probe on out_5
  // Probe on out_6
  // Probe on out_7
  // Probe on out_8

  assign out_3[1] = 1'b0;

  // Notes on the sheet:
  //   R2
  //   R1
  //   ALU OP
  //   L
  //   On
  //   R
  //   R
  //   On
  //   R
  //   A
  //   On
  //   R
  //   S0
  //   On
  //   R
  //   S1
  //   On
  //   R
endmodule

module DPath_STOP (
  input  [7:0] in_1,
  input  [3:0] in_2,
  output out_3
);

  wire and_1_out, decoder_1_out5;
  wire [7:0] not_1_out;

  Decoder #(.select(4)) decoder_1 (
    .out5(decoder_1_out5), .sel(in_2));  // open: out0, out1, out2, out3, out4, out6, out7, out8, out9, out10, out11, out12, out13, out14, out15, en
  assign not_1_out = ~in_1;  // NOT_Gate not_1, 8 bits wide
  and and_1 (and_1_out, ~not_1_out[7], ~not_1_out[6], ~not_1_out[5], ~not_1_out[4], ~not_1_out[3], ~not_1_out[2], ~not_1_out[1], ~not_1_out[0]);  // AND_Gate
  and and_2 (out_3, and_1_out, decoder_1_out5);

  // Notes on the sheet:
  //   STOP
endmodule

module DPath_BRANCH (
  input  [7:0] in_1,
  input  [3:0] in_2,
  input  ALU_ZERO,
  output [7:0] out_4,
  output [1:0] out_5,
  output [1:0] out_6,
  output [1:0] out_7,
  output [1:0] out_8,
  output [1:0] out_9,
  output [1:0] out_10,
  output out_11
);

  wire A, and_6_out, and_7_out, and_8_out, and_10_out, and_11_out, and_12_out, and_13_out, B, BEQ_out,
       BNE_out, BNQ_out, C, D, decoder_1_out5, decoder_1_out6, decoder_1_out7, decoder_1_out8, EQ_out,
       EQUALS_out, NEQ_out, or_1_out, or_2_out;
  wire [7:0] bit_extender_1_out;

  and BNE (BNE_out, in_1[7], in_1[6]);
  buf and_1 (D, in_1[1]);  // AND_Gate
  buf and_2 (C, ~in_1[1]);  // AND_Gate AND_Gate
  and BEQ (BEQ_out, ~in_1[6], in_1[7]);  // AND_Gate
  buf and_3 (A, ~in_1[0]);  // AND_Gate AND_Gate
  Decoder #(.select(4)) decoder_1 (
    .out5(decoder_1_out5), .out6(decoder_1_out6), .out7(decoder_1_out7), .out8(decoder_1_out8), .sel(in_2));  // open: out0, out1, out2, out3, out4, out9, out10, out11, out12, out13, out14, out15, en
  buf and_4 (B, in_1[0]);  // AND_Gate
  or or_1 (or_1_out, BEQ_out, BNE_out);
  and and_5 (out_11, decoder_1_out8, or_1_out);
  // Probe on in_1[5:2]
  and and_6 (and_6_out, decoder_1_out5, or_1_out);
  and and_7 (and_7_out, decoder_1_out6, or_1_out);
  and and_8 (and_8_out, decoder_1_out7, or_1_out);
  assign bit_extender_1_out = {{4{1'b0}}, in_1[5:2]};  // Bit_Extender bit_extender_1
  assign out_4 = or_2_out ? bit_extender_1_out : 8'bz;  // Controlled_Buffer controlled_buffer_1
  or or_2 (or_2_out, EQ_out, NEQ_out);
  and EQ (EQ_out, BEQ_out, and_8_out, ALU_ZERO);
  and NEQ (NEQ_out, BNE_out, and_8_out, ~ALU_ZERO);  // AND_Gate
  and and_9 (out_5[0], and_8_out, or_1_out);
  and EQUALS (EQUALS_out, ALU_ZERO, and_8_out, BEQ_out);
  and BNQ (BNQ_out, ~ALU_ZERO, and_8_out, BNE_out);  // AND_Gate
  and and_10 (and_10_out, A, and_6_out);
  and and_11 (and_11_out, and_7_out, C);
  and and_12 (and_12_out, B, and_6_out);
  and and_13 (and_13_out, and_7_out, D);
  buf or_3 (out_6[1], and_6_out);  // OR_Gate
  buf or_4 (out_6[0], and_6_out);  // OR_Gate
  buf or_5 (out_7[1], and_7_out);  // OR_Gate
  buf or_6 (out_7[0], and_7_out);  // OR_Gate
  or or_7 (out_8[1], and_10_out, and_11_out);
  or or_8 (out_9[1], and_12_out, and_13_out);
  or or_9 (out_10[1], BNQ_out, EQUALS_out);
  or or_10 (out_10[0], BNQ_out, EQUALS_out);
  // Probe on {1'b0, out_5[0]}
  // Probe on out_6
  // Probe on out_7
  // Probe on {out_8[1], 1'b0}
  // Probe on {out_9[1], 1'b0}
  // Probe on out_10

  assign out_5[1] = 1'b0;
  assign out_8[0] = 1'b0;
  assign out_9[0] = 1'b0;

  // Notes on the sheet:
  //   R2
  //   R1
  //   ALU OP
  //   L
  //   On
  //   R
  //   R
  //   On
  //   R
  //   S0
  //   On
  //   R
  //   s1
  //   On
  //   R
  //   pc
  //   On
  //   R
endmodule

module PROGRAMROM (
  input  ROM_INPUT,
  input  clk,
  input  in_3,
  output [7:0] DATA,
  output [3:0] out_5,
  output out_6,
  output [1:0] out_7
);

  wire and_1_out, and_2_out, and_3_out, and_4_out, and_5_out, and_6_out;
  wire [3:0] j_k_ff_1_q;
  wire [7:0] multiplexer_1_out;

  and and_1 (and_1_out, clk, ROM_INPUT, ~out_6);  // AND_Gate
  Multiplexer #(.select(4), .width(8), .enable("false")) multiplexer_1 (
    .in0(8'h10), .in1({8{1'b0}}), .in2({8{1'b0}}), .in3(8'h1), .in4(8'h42), .in5(8'h41), .in6(8'h12),
    .in7(8'h62), .in8(8'h44), .in9(8'h47), .in10(8'h12), .in11(8'h64), .in12(8'h9), .in13(8'hd2),
    .in14(8'h42), .in15(8'hc), .out(multiplexer_1_out), .sel(j_k_ff_1_q));
  J_K_Flip_Flop j_k_ff_1 (.J(1'b1), .K(1'b1), .clk(and_1_out), .Q(j_k_ff_1_q[0]), .reset(in_3));  // open: Qn, preset
  J_K_Flip_Flop j_k_ff_2 (
    .J(j_k_ff_1_q[0]), .K(j_k_ff_1_q[0]), .clk(and_1_out), .Q(j_k_ff_1_q[1]), .reset(in_3));  // open: Qn, preset
  // Probe on j_k_ff_1_q
  and and_2 (and_2_out, j_k_ff_1_q[0], j_k_ff_1_q[1]);
  J_K_Flip_Flop j_k_ff_3 (
    .J(and_2_out), .K(and_2_out), .clk(and_1_out), .Q(j_k_ff_1_q[2]), .reset(in_3));  // open: Qn, preset
  and and_3 (and_3_out, and_2_out, j_k_ff_1_q[2]);
  J_K_Flip_Flop j_k_ff_4 (
    .J(and_3_out), .K(and_3_out), .clk(and_1_out), .Q(j_k_ff_1_q[3]), .reset(in_3));  // open: Qn, preset
  and and_4 (and_4_out, ROM_INPUT, ~out_6);  // AND_Gate
  and and_5 (and_5_out, and_3_out, j_k_ff_1_q[3]);
  assign DATA = and_4_out ? multiplexer_1_out : 8'bz;  // Controlled_Buffer controlled_buffer_1
  J_K_Flip_Flop j_k_ff_5 (.J(and_5_out), .K(and_5_out), .clk(and_1_out), .Q(out_6), .reset(in_3));  // open: Qn, preset
  assign out_5 = and_6_out ? j_k_ff_1_q : 4'bz;  // Controlled_Buffer controlled_buffer_2
  and and_6 (and_6_out, ROM_INPUT, ~out_6);  // AND_Gate
  not not_1 (out_7[1], out_6);

  assign out_7[0] = out_7[1];

  // Notes on the sheet:
  //   Address
  //   ROM DONE
  //   RAM CONTROL
endmodule

module CLOCKCONTROL (
  input  in_1,
  input  ROM_STATUS,
  input  ROM_ON,
  input  STOP,
  output out_5,
  output ROM_CLOCK
);

  wire and_1_out, and_2_out, and_3_out, or_1_out;

  and and_1 (and_1_out, ROM_STATUS, ROM_ON, in_1);
  and and_2 (and_2_out, ~ROM_ON, in_1);  // AND_Gate
  and and_3 (and_3_out, ~ROM_STATUS, ROM_ON, in_1);  // AND_Gate
  or or_1 (or_1_out, and_1_out, and_2_out);
  and and_4 (out_5, ~STOP, or_1_out);  // AND_Gate
  and and_5 (ROM_CLOCK, ~STOP, and_3_out);  // AND_Gate

  // Notes on the sheet:
  //   CLK
  //   SYSTEM CLOCK
endmodule
