// Logisim project Four_Bits_Add_Sub.circ as structural Verilog: 2 circuits, main circuit Add_Sub_4Bits
module Add_Sub_4Bits (
  input  [3:0] B,
  input  [3:0] A,
  input  Add_Sub,
  output Overflow,
  output [3:0] R,
  output Zero
);

  wire add_1bit_2_cout, add_1bit_3_cout, add_1bit_4_cout, or_1_out, xor_1_out, xor_2_out, xor_3_out,
       xor_4_out;

  // Probe on B
  xor xor_1 (xor_1_out, B[3], Add_Sub);
  Add_1Bit add_1bit_1 (.Cout(Overflow), .Sum(R[3]), .B(xor_1_out), .A(A[3]), .Cin(add_1bit_2_cout));
  xor xor_2 (xor_2_out, B[2], Add_Sub);
  Add_1Bit add_1bit_2 (.Cout(add_1bit_2_cout), .Sum(R[2]), .B(xor_2_out), .A(A[2]), .Cin(add_1bit_3_cout));
  xor xor_3 (xor_3_out, B[1], Add_Sub);
  Add_1Bit add_1bit_3 (.Cout(add_1bit_3_cout), .Sum(R[1]), .B(xor_3_out), .A(A[1]), .Cin(add_1bit_4_cout));
  // Probe on R
  // Probe on A
  xor xor_4 (xor_4_out, B[0], Add_Sub);
  Add_1Bit add_1bit_4 (.Cout(add_1bit_4_cout), .Sum(R[0]), .B(xor_4_out), .A(A[0]), .Cin(Add_Sub));
  not not_1 (Zero, or_1_out);
  or or_1 (or_1_out, R[0], R[1], R[2], R[3]);

  // Notes on the sheet:
  //   Wei Zhe Ni 260674646
  //   MAKE SURE THAT YOU OPENED THIS PROJECT IN "LOGISIM-EVOLUTION"
  //   YOU CAN FIND "LOGISIM-EVOLUTION" PRORAM IN THE ASSIGNMENT'S FOLDER
  //   DO NOT USE "LOGISIM" VERSION TO SOLVE THIS ASSIGNMENT!
endmodule

module Add_1Bit (
  input  Cin,
  input  A,
  input  B,
  output Sum,
  output Cout
);

  wire and_1_out, and_2_out, and_3_out, and_4_out, and_5_out, and_6_out, and_7_out, not_1_out, not_2_out,
       not_3_out;

  not not_1 (not_1_out, Cin);
  not not_2 (not_2_out, A);
  not not_3 (not_3_out, B);
  and and_1 (and_1_out, not_2_out, not_3_out, Cin, Cin);
  and and_2 (and_2_out, not_2_out, B, B, not_1_out);
  and and_3 (and_3_out, A, not_3_out, not_1_out);
  and and_4 (and_4_out, A, B, Cin);
  and and_5 (and_5_out, B, Cin);
  and and_6 (and_6_out, A, Cin);
  and and_7 (and_7_out, A, B);
  or or_1 (Sum, and_1_out, and_2_out, and_3_out, and_4_out);
  or or_2 (Cout, and_5_out, and_6_out, and_7_out);

  // Notes on the sheet:
  //   Wei Zhe Ni 260674646
  //   MAKE SURE THAT YOU OPENED THIS PROJECT IN "LOGISIM-EVOLUTION"
  //   YOU CAN FIND "LOGISIM-EVOLUTION" PRORAM IN THE ASSIGNMENT'S FOLDER
  //   DO NOT USE "LOGISIM" VERSION TO SOLVE THIS ASSIGNMENT!
endmodule
